# Fritzing sketch circDiagramF (saved by Fritzing 0.9.3b)

parts:
  M1 = DOIT Esp32 DevKit v1 (30 pins long, 11 pins width) [part_number=ESP32S-PIN30]
  TFT1 = 2.2" TFT with MicroSD Breakout
  Part1 = Real Time Clock Module - DS1307 RTC Breakout Board
  U1 = RF-LINK_RX [package=rf-link_rx]
  DHT11_1 = DHT11 module

nets:
  3V3: M1.3V3, TFT1.VIN, Part1.5V, DHT11_1.VCC
  GND: M1.GND, TFT1.GND, Part1.GND, U1.GND, DHT11_1.GND
  N1: M1.D4, U1.DATA
  N2: M1.RX2, TFT1.SDCS
  N3: M1.TX2, TFT1.CS
  N4: M1.D5, TFT1.RST
  N5: M1.D18, TFT1.SCK
  N6: M1.D19, TFT1.MISO
  N7: M1.D21, Part1.SDA
  N8: M1.D22, Part1.SCL
  N9: M1.D23, TFT1.MOSI
  N10: M1.D32, DHT11_1.DATA
  N11: M1.D27, TFT1.BL

custom parts:
  DOIT Esp32 DevKit v1 (30 pins long, 11 pins width): The DOIT Esp32 DevKit v1 is one of the development board created by DOIT to evaluate the ESP-WROOM-32 module. It is based on the ESP32 microcontroller that boasts Wifi, Bluetooth, Ethernet and Low Power support all in a single chip. (vanepp) made breadboard work, adjusted pin numbering and labels and reduced size of schematic and cleaned up pcb. This chip is 30pins long (2 x15) and 11 pins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
  2.2" TFT with MicroSD Breakout: 2.2" TFT Display with HX8340B Controller and MicroSD Card
  DHT11 module: DHT11 black pcb module
